# Fritzing sketch Ghostblasters (saved by Fritzing 0.9.3b)
breadboards: 2

parts:
  R1 = Photocell (LDR) [package=THT]
  R2 = Resistor [tolerance=±5% resistance=100k package="2512 [SMD]"]
  R3 = Photocell (LDR) [package=THT]
  R4 = Resistor [tolerance=±5% resistance=100k package="2512 [SMD]"]
  R5 = Photocell (LDR) [package=THT]
  R6 = Resistor [tolerance=±5% resistance=100k package="2512 [SMD]"]
  R7 = Photocell (LDR) [package=THT]
  R8 = Resistor [tolerance=±5% resistance=100k package="2512 [SMD]"]
  R9 = Photocell (LDR) [package=THT]
  R10 = Resistor [tolerance=±5% resistance=100k package="2512 [SMD]"]
  R11 = Photocell (LDR) [package=THT]
  R12 = Resistor [tolerance=±5% resistance=100k package="2512 [SMD]"]
  Part2 = Arduino Mega 2560 (Rev3)
  M8 = Dagu DGServo 9g (Top view) [part_number=RS001B]
  M9 = Dagu DGServo 9g (Top view) [part_number=RS001B]
  M10 = Dagu DGServo 9g (Top view) [part_number=RS001B]
  M11 = Dagu DGServo 9g (Top view) [part_number=RS001B]
  M12 = Dagu DGServo 9g (Top view) [part_number=RS001B]
  M13 = Dagu DGServo 9g (Top view) [part_number=RS001B]
  U1 = 7-SEGMENT-4DIGIT [package=7-segment-4digit]
  R21 = Resistor [tolerance=±5% resistance=220 package="2512 [SMD]"]
  R22 = Resistor [tolerance=±5% resistance=220 package="2512 [SMD]"]
  R23 = Resistor [tolerance=±5% resistance=220 package="2512 [SMD]"]
  R24 = Resistor [tolerance=±5% resistance=220 package="2512 [SMD]"]
  R25 = Resistor [tolerance=±5% resistance=220 package="2512 [SMD]"]
  R26 = Resistor [tolerance=±5% resistance=220 package="2512 [SMD]"]
  R27 = Resistor [tolerance=±5% resistance=220 package="2512 [SMD]"]
  R28 = Resistor [tolerance=±5% resistance=220 package="2512 [SMD]"]
  Mod1 = Heltec WiFi Kit 8 [part_number=HTIT-W8266]
  Mod2 = KY-008 Laser Transmitter Module [package="Breakout board"]
  S1 = Pushbutton [package=THT]
  S2 = Pushbutton [package=THT]
  IR1 = TSOP312.., 314.. [package=THT]
  U2 = Vibration Motor- ROB-08449 [package=vibe-motor-10mm]  # not connected
  D1 = LTE-302 [package=lte-302]
  R29 = Resistor [tolerance=±5% resistance=330 package="0603 [SMD]"]
  DFRobot_DFPlayer_Mini1 = DFRobot DFPlayer Mini [part_number=DFR0299]
  SP1 = SPEAKER [package=pcb_mount_speaker]
  R30 = Resistor [tolerance=±5% resistance=1k package="0603 [SMD]"]
  VCC1 = 4 x AAA Battery Mount

nets:
  N1: R1.pin_0, R2.Pin_0
  5V: R1.pin_1, R3.pin_1, R5.pin_1, R7.pin_1, R9.pin_1, R11.pin_1, Part2.5V, Part2.D23, Part2.D27, Part2.D31, IR1.Data, DFRobot_DFPlayer_Mini1.VCC
  N2: R2.Pin_1, R4.Pin_1, R6.Pin_1, R8.Pin_1, R10.Pin_1, R12.Pin_1, Part2.GND, IR1.Vs, DFRobot_DFPlayer_Mini1.GND-1
  N3: R3.pin_0, R4.Pin_0
  N4: R5.pin_0, R6.Pin_0
  N5: R7.pin_0, R8.Pin_0, Part2.D33
  N6: R9.pin_0, R10.Pin_0
  N7: R11.pin_0, R12.Pin_0, Part2.D25
  N8: Part2.D13_PWM, U1.6
  N9: Part2.D12_PWM, U1.16
  N10: Part2.D11_PWM, U1.13
  N11: Part2.D9_PWM, IR1.GND
  N12: Part2.D2_PWM, M10.pulse
  N13: Part2.D3_PWM, M9.pulse
  N14: Part2.D4_PWM, M13.pulse
  N15: Part2.D5_PWM, M12.pulse
  N16: Part2.D6_PWM, M11.pulse
  N17: Part2.D7_PWM, M8.pulse
  N18: Part2.D35, R28.Pin_1
  N19: Part2.D37, R27.Pin_1
  N20: Part2.D39, R26.Pin_1
  N21: Part2.D41, R23.Pin_1
  N22: Part2.D43, R25.Pin_1
  N23: Part2.D45, R22.Pin_1
  N24: Part2.D47, R21.Pin_1
  N25: Part2.D49, R24.Pin_1
  N26: Part2.D51, R30.Pin_0
  N27: Part2.D53, DFRobot_DFPlayer_Mini1.TX
  GND: M8.gnd, M9.gnd, M10.gnd, M11.gnd, M12.gnd, M13.gnd, VCC1.-
  VCC: M8.vcc, M9.vcc, M10.vcc, M11.vcc, M12.vcc, M13.vcc, VCC1.+
  N28: U1.1, R23.Pin_0
  N29: U1.2, R25.Pin_0
  N30: U1.3, R28.Pin_0
  N31: U1.4, R22.Pin_0
  N32: U1.5, R27.Pin_0
  N33: U1.11, R21.Pin_0
  N34: U1.14, R26.Pin_0
  N35: U1.15, R24.Pin_0
  N36: Mod1.pin_11, Mod2.NC, S1.leg1, S2.leg1
  N37: Mod1.pin_12, Mod2.-, D1.A
  N38: Mod1.pin_15, Mod1.pin_18, Mod1.pin_19, R29.Pin_1
  N39: Mod1.pin_16, Mod1.pin_21, S2.leg0
  N40: Mod1.pin_17, Mod1.pin_20, Mod2.S, S1.leg0
  N41: D1.C, R29.Pin_0
  N42: DFRobot_DFPlayer_Mini1.RX, R30.Pin_1
  N43: DFRobot_DFPlayer_Mini1.SPK_1, SP1.+
  N44: DFRobot_DFPlayer_Mini1.SPK_2, SP1.-

custom parts:
  Heltec WiFi Kit 8: The Heltec WiFi Kit 8 is an IoT development board designed and produced by Heltec Automation and based on the Espressif ESP8266 processor module. The board includes built-in WiFi, a 0.91″ OLED display and a Li-Po battery management system. Links: Heltec WiFi Kit 32 product page Github
  KY-008 Laser Transmitter Module: KY-008 Laser Transmitter Module, emits a dot shaped red laser beam.
